// Logisim project p2.circ as structural Verilog: 1 circuit, main circuit main
module main (
  input  X,
  input  y,
  output z
);

  wire transistor_3_out;

  Transistor transistor_1 (.in(1'b1), .out(z), .gate(X));
  Transistor #(.\type ("n")) transistor_2 (.in(transistor_3_out), .out(z), .gate(X));
  Transistor #(.\type ("n")) transistor_3 (.in(1'b0), .out(transistor_3_out), .gate(y));
  Transistor transistor_4 (.in(1'b1), .out(z), .gate(y));

  // Notes on the sheet:
  //   VDD
  //   GND
  //   NAND GATE
  //   SIDDHARTH THAKUR
  //   1601CS46
endmodule
