// Logisim project p5.circ as structural Verilog: 6 circuits, main circuit main
module main (
  input  A,
  input  B,
  input  C,
  output OUTPUT
);

  wire and_1_out_3;

  AND and_1 (.X(A), .y(B), .out_3(and_1_out_3));
  OR or_1 (.X(and_1_out_3), .Y(C), .out_3(OUTPUT));

  // Notes on the sheet:
  //   1601CS46
  //   SIDDHARTH THAKUR
endmodule

module NAND (
  input  X,
  input  y,
  output z
);

  wire transistor_3_out;

  Transistor transistor_1 (.in(1'b1), .out(z), .gate(X));
  Transistor #(.\type ("n")) transistor_2 (.in(transistor_3_out), .out(z), .gate(X));
  Transistor #(.\type ("n")) transistor_3 (.in(1'b0), .out(transistor_3_out), .gate(y));
  Transistor transistor_4 (.in(1'b1), .out(z), .gate(y));

  // Notes on the sheet:
  //   VDD
  //   GND
  //   NAND GATE
  //   SIDDHARTH THAKUR
  //   1601CS46
endmodule

module NOR (
  input  X,
  input  Y,
  output Z
);

  wire transistor_2_out;

  Transistor #(.\type ("n")) transistor_1 (.in(1'b0), .out(Z), .gate(X));
  Transistor transistor_2 (.in(1'b1), .out(transistor_2_out), .gate(X));
  Transistor transistor_3 (.in(transistor_2_out), .out(Z), .gate(Y));
  Transistor #(.\type ("n")) transistor_4 (.in(1'b0), .out(Z), .gate(Y));

  // Notes on the sheet:
  //   VDD
  //   GND
  //   NOR GATE
  //   SIDDHART THAKUR
  //   1601CS46
  //   ~(X+Y)
endmodule

module AND (
  input  X,
  input  y,
  output out_3
);

  wire transistor_1_out, transistor_3_out;

  Transistor transistor_1 (.in(1'b1), .out(transistor_1_out), .gate(X));
  Transistor #(.\type ("n")) transistor_2 (.in(transistor_3_out), .out(transistor_1_out), .gate(X));
  Transistor #(.\type ("n")) transistor_3 (.in(1'b0), .out(transistor_3_out), .gate(y));
  Transistor transistor_4 (.in(1'b1), .out(transistor_1_out), .gate(y));
  Transistor transistor_5 (.in(1'b1), .out(out_3), .gate(transistor_1_out));
  Transistor #(.\type ("n")) transistor_6 (.in(1'b0), .out(out_3), .gate(transistor_1_out));

  // Notes on the sheet:
  //   VDD
  //   GND
  //   AND GATE
  //   SIDDHARTH THAKUR
  //   1601CS46
endmodule

module OR (
  input  X,
  input  Y,
  output out_3
);

  wire transistor_1_out, transistor_2_out;

  Transistor #(.\type ("n")) transistor_1 (.in(1'b0), .out(transistor_1_out), .gate(X));
  Transistor transistor_2 (.in(1'b1), .out(transistor_2_out), .gate(X));
  Transistor transistor_3 (.in(transistor_2_out), .out(transistor_1_out), .gate(Y));
  Transistor #(.\type ("n")) transistor_4 (.in(1'b0), .out(transistor_1_out), .gate(Y));
  Transistor transistor_5 (.in(1'b1), .out(out_3), .gate(transistor_1_out));
  Transistor #(.\type ("n")) transistor_6 (.in(1'b0), .out(out_3), .gate(transistor_1_out));

  // Notes on the sheet:
  //   VDD
  //   GND
  //   1601CS46
  //   OR GATE
  //   SIDDHART THAKUR
  //   ~(X+Y)
endmodule

module XOR (
  input  A,
  input  B,
  output OUTPUT
);

  wire transistor_1_out, transistor_3_out, transistor_5_out, transistor_8_out, transistor_9_out,
       transistor_12_out;

  Transistor transistor_1 (.in(1'b1), .out(transistor_1_out), .gate(A));
  Transistor #(.\type ("n")) transistor_2 (.in(1'b0), .out(transistor_1_out), .gate(A));
  Transistor transistor_3 (.in(1'b1), .out(transistor_3_out), .gate(B));
  Transistor #(.\type ("n")) transistor_4 (.in(1'b0), .out(transistor_3_out), .gate(B));
  Transistor transistor_5 (.in(1'b1), .out(transistor_5_out), .gate(transistor_1_out));
  Transistor transistor_6 (.in(transistor_5_out), .out(OUTPUT), .gate(B));
  Transistor #(.\type ("n")) transistor_7 (.in(transistor_8_out), .out(OUTPUT), .gate(A));
  Transistor #(.\type ("n")) transistor_8 (.in(1'b0), .out(transistor_8_out), .gate(B));
  Transistor transistor_9 (.in(1'b1), .out(transistor_9_out), .gate(A));
  Transistor transistor_10 (.in(transistor_9_out), .out(OUTPUT), .gate(transistor_3_out));
  Transistor #(.\type ("n")) transistor_11 (.in(transistor_12_out), .out(OUTPUT), .gate(transistor_1_out));
  Transistor #(.\type ("n")) transistor_12 (.in(1'b0), .out(transistor_12_out), .gate(transistor_3_out));

  // Notes on the sheet:
  //   INPUTS
  //   A XOR B
  //   1601CS46
  //   GND
  //   SIDDHARTH THAKUR
  //   VDD
  //   A.~B + ~A.B
endmodule
