// Logisim project p9.circ as structural Verilog: 3 circuits, main circuit main
module main (
  input  b0,
  input  a0,
  input  b1,
  input  a1,
  output s0,
  output s1,
  output c
);

  wire half_adder_1_carry;

  Half_Adder half_adder_1 (.A(a0), .B(b0), .SUM(s0), .CARRY(half_adder_1_carry));
  Full_Adder full_adder_1 (.A(a1), .B(b1), .C(half_adder_1_carry), .SUM(s1), .CARRY(c));
endmodule

module Half_Adder (
  input  A,
  input  B,
  output SUM,
  output CARRY
);

  xor xor_1 (SUM, A, B);
  and and_1 (CARRY, A, B);
endmodule

module Full_Adder (
  input  A,
  input  B,
  input  C,
  output SUM,
  output CARRY
);

  wire and_1_out, and_2_out, and_3_out, and_4_out, and_5_out, and_6_out, and_7_out, not_1_out, not_2_out,
       not_3_out, not_4_out, not_5_out, not_6_out;

  not not_1 (not_1_out, A);
  not not_2 (not_2_out, B);
  not not_3 (not_3_out, A);
  not not_4 (not_4_out, C);
  not not_5 (not_5_out, B);
  not not_6 (not_6_out, C);
  and and_1 (and_1_out, B, C);
  and and_2 (and_2_out, A, C);
  and and_3 (and_3_out, A, B);
  and and_4 (and_4_out, not_3_out, B, not_4_out);
  and and_5 (and_5_out, A, not_5_out, not_6_out);
  and and_6 (and_6_out, not_1_out, not_2_out, C);
  and and_7 (and_7_out, A, B, C);
  or or_1 (CARRY, and_1_out, and_2_out, and_3_out);
  or or_2 (SUM, and_6_out, and_4_out, and_5_out, and_7_out);
endmodule
