// Logisim project p1.circ as structural Verilog: 2 circuits, main circuit main
module main (
  input  C,
  input  A,
  input  B,
  output SUM,
  output CARRY
);

  wire not_1_out;

  not not_1 (not_1_out, C);
  _4_to_MUX u_4_to_mux_1 (.in_1(C), .in_2(not_1_out), .in_3(not_1_out), .in_4(C), .in_5(A), .in_6(B), .out_7(SUM));
  _4_to_MUX u_4_to_mux_2 (.in_1(1'b0), .in_2(C), .in_3(C), .in_4(1'b1), .in_5(A), .in_6(B), .out_7(CARRY));
endmodule

module _4_to_MUX (
  input  in_1,
  input  in_2,
  input  in_3,
  input  in_4,
  input  in_5,
  input  in_6,
  output out_7
);

  wire and_1_out, and_2_out, and_3_out, and_4_out, not_1_out, not_2_out;

  not not_1 (not_1_out, in_5);
  not not_2 (not_2_out, in_6);
  and and_1 (and_1_out, in_1, not_1_out, not_2_out);
  and and_2 (and_2_out, in_2, not_1_out, in_6);
  and and_3 (and_3_out, in_3, in_5, not_2_out);
  and and_4 (and_4_out, in_4, in_5, in_6);
  or or_1 (out_7, and_1_out, and_2_out, and_3_out, and_4_out);
endmodule
