// Logisim project p2.circ as structural Verilog: 3 circuits, main circuit main
module main (
  input  B2,
  input  B1,
  input  B4,
  input  B3,
  input  A1,
  input  C0,
  input  A4,
  input  A2,
  input  A3,
  input  B5,
  input  B8,
  input  B7,
  input  B6,
  input  A7,
  input  A8,
  input  A6,
  input  A5,
  output S3,
  output S1,
  output S4,
  output S2,
  output C4,
  output S7,
  output S5,
  output S8,
  output S6,
  output OVERFLOW
);

  wire full_adder_2_carry, full_adder_3_carry, full_adder_4_carry, full_adder_5_carry, full_adder_6_carry,
       full_adder_7_carry, full_adder_8_carry, xor_1_out, xor_2_out, xor_4_out, xor_5_out, xor_6_out,
       xor_7_out, xor_8_out, xor_9_out, xor_10_out, xor_11_out;

  xor xor_1 (xor_1_out, B8, A8);
  xor xor_2 (xor_2_out, full_adder_2_carry, S8);
  xor xor_3 (OVERFLOW, xor_1_out, xor_2_out);
  xor xor_4 (xor_4_out, B8, C0);
  xor xor_5 (xor_5_out, B4, C0);
  FULL_ADDER full_adder_1 (.A(full_adder_3_carry), .B(A4), .C(xor_5_out), .SUM(S4), .CARRY(C4));
  xor xor_6 (xor_6_out, B7, C0);
  FULL_ADDER full_adder_2 (.A(full_adder_4_carry), .B(A8), .C(xor_4_out), .SUM(S8), .CARRY(full_adder_2_carry));
  xor xor_7 (xor_7_out, B2, C0);
  xor xor_8 (xor_8_out, B3, C0);
  FULL_ADDER full_adder_3 (.A(full_adder_5_carry), .B(A3), .C(xor_8_out), .SUM(S3), .CARRY(full_adder_3_carry));
  xor xor_9 (xor_9_out, B6, C0);
  FULL_ADDER full_adder_4 (.A(full_adder_6_carry), .B(A7), .C(xor_6_out), .SUM(S7), .CARRY(full_adder_4_carry));
  FULL_ADDER full_adder_5 (.A(full_adder_7_carry), .B(A2), .C(xor_7_out), .SUM(S2), .CARRY(full_adder_5_carry));
  xor xor_10 (xor_10_out, B5, C0);
  FULL_ADDER full_adder_6 (.A(full_adder_8_carry), .B(A6), .C(xor_9_out), .SUM(S6), .CARRY(full_adder_6_carry));
  xor xor_11 (xor_11_out, B1, C0);
  FULL_ADDER full_adder_7 (.A(C0), .B(A1), .C(xor_11_out), .SUM(S1), .CARRY(full_adder_7_carry));
  FULL_ADDER full_adder_8 (.A(C4), .B(A5), .C(xor_10_out), .SUM(S5), .CARRY(full_adder_8_carry));

  // Notes on the sheet:
  //   8-bit Adder/Subtractor using dual IC 7483
endmodule

module FULL_ADDER (
  input  A,
  input  B,
  input  C,
  output SUM,
  output CARRY
);

  wire and_1_out, and_2_out, and_3_out, and_4_out, and_5_out, and_6_out, and_7_out, not_1_out, not_2_out,
       not_3_out, not_4_out, not_5_out, not_6_out;

  not not_1 (not_1_out, A);
  not not_2 (not_2_out, B);
  not not_3 (not_3_out, A);
  not not_4 (not_4_out, C);
  not not_5 (not_5_out, B);
  not not_6 (not_6_out, C);
  and and_1 (and_1_out, B, C);
  and and_2 (and_2_out, A, C);
  and and_3 (and_3_out, A, B);
  and and_4 (and_4_out, not_3_out, B, not_4_out);
  and and_5 (and_5_out, A, not_5_out, not_6_out);
  and and_6 (and_6_out, not_1_out, not_2_out, C);
  and and_7 (and_7_out, A, B, C);
  or or_1 (CARRY, and_1_out, and_2_out, and_3_out);
  or or_2 (SUM, and_6_out, and_4_out, and_5_out, and_7_out);
endmodule

module _4_bit_add_subt (
  input  B4,
  input  B3,
  input  B2,
  input  B1,
  input  C0,
  input  A4,
  input  A3,
  input  A2,
  input  A1,
  output C4,
  output S4,
  output S3,
  output S2,
  output S1
);

  wire full_adder_2_carry, full_adder_3_carry, full_adder_4_carry, xor_1_out, xor_2_out, xor_3_out, xor_4_out;

  xor xor_1 (xor_1_out, B4, C0);
  FULL_ADDER full_adder_1 (.A(full_adder_2_carry), .B(A4), .C(xor_1_out), .SUM(S4), .CARRY(C4));
  xor xor_2 (xor_2_out, B2, C0);
  xor xor_3 (xor_3_out, B3, C0);
  FULL_ADDER full_adder_2 (.A(full_adder_3_carry), .B(A3), .C(xor_3_out), .SUM(S3), .CARRY(full_adder_2_carry));
  FULL_ADDER full_adder_3 (.A(full_adder_4_carry), .B(A2), .C(xor_2_out), .SUM(S2), .CARRY(full_adder_3_carry));
  xor xor_4 (xor_4_out, B1, C0);
  FULL_ADDER full_adder_4 (.A(C0), .B(A1), .C(xor_4_out), .SUM(S1), .CARRY(full_adder_4_carry));
endmodule
