// Logisim project p1.circ as structural Verilog: 1 circuit, main circuit main
module main (
  input  in_1,
  input  in_2,
  output out_3,
  output out_4,
  output out_5,
  output out_6,
  output out_7,
  output out_8,
  output out_9,
  output out_10
);

  wire clock_1_out;

  Clock clock_1 (.out(clock_1_out));
  Register #(.width(1)) register_1 (.D(out_4), .en(in_1), .Q(out_3), .clk(clock_1_out));  // open: clr
  Register #(.width(1), .trigger("falling")) register_2 (
    .D(out_5), .en(in_1), .Q(out_4), .clk(clock_1_out));  // open: clr
  Register #(.width(1)) register_3 (.D(out_6), .en(in_1), .Q(out_5), .clk(clock_1_out));  // open: clr
  Register #(.width(1)) register_4 (.D(out_7), .en(in_1), .Q(out_6), .clk(clock_1_out));  // open: clr
  Register #(.width(1)) register_5 (.D(out_8), .en(in_1), .Q(out_7), .clk(clock_1_out));  // open: clr
  Register #(.width(1)) register_6 (.D(out_9), .en(in_1), .Q(out_8), .clk(clock_1_out));  // open: clr
  Register #(.width(1)) register_7 (.D(out_10), .en(in_1), .Q(out_9), .clk(clock_1_out));  // open: clr
  Register #(.width(1)) register_8 (.D(in_2), .en(in_1), .Q(out_10), .clk(clock_1_out));  // open: clr
endmodule
