// Logisim project counter.circ as structural Verilog: 1 circuit, main circuit main
module main (
  input  in_1,
  input  in_2,
  output out_3,
  output out_4
);

  wire and_1_out, and_2_out, and_3_out, clock_1_out, not_1_out, or_1_out, or_2_out, xor_1_out;

  Clock clock_1 (.out(clock_1_out));
  xor xor_1 (xor_1_out, in_1, in_2);
  not not_1 (not_1_out, out_4);
  T_Flip_Flop t_ff_1 (.clk(clock_1_out), .T(xor_1_out), .Q(out_4));  // open: Qn, preset, reset, en
  and and_1 (and_1_out, in_2, out_4);
  and and_2 (and_2_out, in_1, not_1_out);
  and and_3 (and_3_out, in_2, in_1);
  or or_1 (or_1_out, and_1_out, and_2_out);
  T_Flip_Flop t_ff_2 (.clk(clock_1_out), .T(or_2_out), .Q(out_3));  // open: Qn, preset, reset, en
  or or_2 (or_2_out, or_1_out, and_3_out);
endmodule
