// Logisim project p1.circ as structural Verilog: 6 circuits, main circuit main
module main (
  input  A,
  input  B,
  input  C,
  output SUM,
  output CARRY
);

  wire and_gate_1_output, and_gate_2_output, and_gate_3_output, or_gate_1_output, xor_gate_1_y;

  XOR_gate xor_gate_1 (.A(A), .B(B), .Y(xor_gate_1_y));
  XOR_gate xor_gate_2 (.A(xor_gate_1_y), .B(C), .Y(SUM));
  AND_gate and_gate_1 (.A(A), .B(B), .OUTPUT(and_gate_1_output));
  AND_gate and_gate_2 (.A(B), .B(C), .OUTPUT(and_gate_2_output));
  AND_gate and_gate_3 (.A(C), .B(A), .OUTPUT(and_gate_3_output));
  OR_gate or_gate_1 (.A(and_gate_1_output), .B(and_gate_2_output), .OUTPUT(or_gate_1_output));
  OR_gate or_gate_2 (.A(or_gate_1_output), .B(and_gate_3_output), .OUTPUT(CARRY));

  // Notes on the sheet:
  //   FULL ADDER
endmodule

module NOR_gate (
  input  A,
  input  B,
  output OUTPUT
);

  wire nand_1_out, nand_2_out, nand_3_out;

  nand nand_1 (nand_1_out, A, A);
  nand nand_2 (nand_2_out, B, B);
  nand nand_3 (nand_3_out, nand_1_out, nand_2_out);
  nand nand_4 (OUTPUT, nand_3_out, nand_3_out);
endmodule

module OR_gate (
  input  A,
  input  B,
  output OUTPUT
);

  wire nand_1_out, nand_2_out;

  nand nand_1 (nand_1_out, A, A);
  nand nand_2 (nand_2_out, B, B);
  nand nand_3 (OUTPUT, nand_1_out, nand_2_out);
endmodule

module NOT_gate (
  input  A,
  output OUTPUT
);

  nand nand_1 (OUTPUT, A, A);
endmodule

module AND_gate (
  input  A,
  input  B,
  output OUTPUT
);

  wire nand_1_out;

  nand nand_1 (nand_1_out, A, B);
  nand nand_2 (OUTPUT, nand_1_out, nand_1_out);
endmodule

module XOR_gate (
  input  A,
  input  B,
  output Y
);

  wire nand_1_out, nand_2_out, nand_3_out, nand_4_out;

  nand nand_1 (nand_1_out, A, A);
  nand nand_2 (nand_2_out, B, B);
  nand nand_3 (nand_3_out, A, nand_2_out);
  nand nand_4 (nand_4_out, nand_1_out, B);
  nand nand_5 (Y, nand_3_out, nand_4_out);
endmodule
