// Logisim project p4.circ as structural Verilog: 1 circuit, main circuit main
module main (
  input  A,
  input  B,
  input  C,
  input  D,
  output Z,
  output Y
);

  wire and_1_out, and_2_out, and_3_out, and_4_out, and_5_out, not_1_out, not_2_out, not_3_out, not_4_out;

  not not_1 (not_1_out, A);
  not not_2 (not_2_out, B);
  not not_3 (not_3_out, C);
  not not_4 (not_4_out, D);
  and and_1 (and_1_out, not_1_out, D);
  and and_2 (and_2_out, B, D);
  and and_3 (and_3_out, A, not_3_out, D);
  and and_4 (and_4_out, A, not_2_out, C);
  and and_5 (and_5_out, A, B, C, D);
  or or_1 (Y, and_1_out, and_3_out, and_4_out, and_5_out);
  or or_2 (Z, and_2_out, and_3_out);

  // Notes on the sheet:
  //   SIDDHARTH THAKUR (1601CS46)
endmodule
