// Logisim project p5.circ as structural Verilog: 1 circuit, main circuit main
module main (
  input  A0,
  input  A1,
  input  A2,
  input  A3,
  output Y0,
  output Y1,
  output Y2,
  output Y3
);

  wire not_1_out, not_2_out, not_3_out;

  not not_1 (not_1_out, A1);
  not not_2 (not_2_out, A2);
  not not_3 (not_3_out, A3);
  and and_1 (Y0, A0, not_1_out, not_2_out, not_3_out);
  and and_2 (Y1, A1, not_2_out, not_3_out);
  and and_3 (Y2, A2, not_3_out);

  assign Y3 = A3;

  // Notes on the sheet:
  //   1601CS46
  //   SIDDHARTH THAKUR
endmodule
